# Fritzing sketch IREmitterDetector (saved by Fritzing 0.7.11b)
breadboards: 1

parts:
  Q1 = NPN-Transistor [package="TO92 [THT]"]
  R1 = Resistor [tolerance=±5% resistance=47 package=THT]
  IR_Emitter = LED - 5mm [color="Infrared (850nm)" package="5 mm [THT]"]
  R3 = Resistor [tolerance=±5% resistance=100 package=THT]
  R4 = Resistor [tolerance=±5% resistance=1k package=THT]
  Emitter_Indicator = LED - 5mm [color="Green (555nm)" package="5 mm [THT]"]
  Q2 = PNP-Transistor [package="TO92 [THT]"]
  R7 = Resistor [tolerance=±5% resistance=1k package=THT]
  Threshold_Indicator = LED - 5mm [color="Red (633nm)" package="5 mm [THT]"]
  R6 = Resistor [tolerance=±5% resistance=100k package=THT]
  IR_Detector = LED - 5mm [color="Infrared (850nm)" package="5 mm [THT]"]
  Threshold_Trim_(R5) = Trimmer Potentiometer [maximum_resistance=10kΩ package=THT]
  Arduino1 = Arduino

nets:
  N1: Q1.E, R4.Pin_0
  N2: Q1.B, R3.Pin_1
  N3: Q1.C, IR_Emitter.cathode
  N4: R1.Pin_0, Q2.C, Threshold_Trim_(R5).leg2, Arduino1.+5V
  N5: R1.Pin_1, IR_Emitter.anode
  N6: R3.Pin_0, Arduino1.D9
  N7: R4.Pin_1, Emitter_Indicator.anode
  N8: Emitter_Indicator.cathode, Threshold_Indicator.cathode, IR_Detector.anode, Threshold_Trim_(R5).leg1, Arduino1.GND
  N9: Q2.E, R7.Pin_0
  N10: Q2.B, R6.Pin_1
  N11: R7.Pin_1, Threshold_Indicator.anode
  N12: R6.Pin_0, IR_Detector.cathode, Arduino1.A0
  N13: Threshold_Trim_(R5).wiper, Arduino1.A1
